# Fritzing sketch Circuit (saved by Fritzing 0.9.2b)
circuit board: 8.46667cm x 5.64444cm
breadboards: 1

parts:
  IC1 = IC, DIP package, 8 pins [chip_label=ATTiny85]
  R1 = Resistor [tolerance=±5% resistance=10k package=THT]
  CdS = Photocell (LDR) [package=THT]
  R3 = Resistor [tolerance=±5% resistance=330 package=THT]
  LED1 = LED - 5mm [color="White (6500K)" current=30mA package="5 mm [THT]"]
  10K_Pot = Breadboard Trimpot
  S1 = Pushbutton [package=THT]

nets:
  N1: IC1.pin2, 10K_Pot.PIN3
  N2: IC1.pin3, 10K_Pot.PIN2
  GND: IC1.pin4, R1.Pin_0, LED1.cathode, 10K_Pot.PIN1, S1.leg1
  N3: IC1.pin5, R3.Pin_0
  N4: IC1.pin6, S1.leg0
  N5: IC1.pin7, R1.Pin_1, CdS.pin_1
  5V: IC1.pin8, CdS.pin_0
  N6: R3.Pin_1, LED1.anode

// code stored in the sketch: Super_Night_Light_Trinket.ino
/******************************************
 *         "Super Night Light"            *
 *    Code and Hardware designed by:      *
 *            David Ockey                 *
 ******************************************
 * Copyright: David Ockey                 *
 ******************************************/
#define CdS 2
#define buttonPin 1
#define KNOB 4
#define LED 0

unsigned int threshold = 150;
boolean trig = false;
boolean buttonStatus = false;
boolean LEDStatus = false;

boolean finish = false;

void setup() {
  pinMode(buttonPin, INPUT);
  pinMode(CdS, INPUT);
  pinMode(3, OUTPUT);
  pinMode(KNOB, INPUT);
  pinMode(LED, OUTPUT);
  
  digitalWrite(3, HIGH);
}

void loop() {
  int input = analogRead(CdS);

  if (digitalRead(buttonPin) == HIGH) {
    if (buttonStatus == false) {
      buttonStatus = true;
      LEDStatus = !LEDStatus;
      if (LEDStatus == false) {
        trig = true;
      }
    }
  }
  else {
    buttonStatus = false;
  }

  if (!LEDStatus && input < threshold && !trig) {
    trig = true;

    for(int fadeValue = 0 ; fadeValue <= 255; fadeValue +=5) { 
      // sets the value (range from 0 to 255):
      analogWrite(LED, fadeValue);
      delay(5);  
    }

    boolean cancel = false;
    for (int i = 0; !cancel && i < 5000; i++) {
      analogWrite(LED, 255);
      
      if (digitalRead(buttonPin) == HIGH) {
        cancel = true;
        LEDStatus = false;
        buttonStatus = true;
      }

      delay(1);
    }

    // fade out from max to min
    for(int fadeValue = 255; !cancel && fadeValue >= 0; fadeValue--) { 
      // sets the value (range from 0 to 255):
      analogWrite(LED, fadeValue);

      // wait for 5 milliseconds to see the dimming effect    
      delay(5);
    }
    
    if (cancel) {
      digitalWrite(LED, LOW);
      delay(500);
    }
    
  }
  else if (input >= threshold) {
    trig = false;
  }
}
