# Fritzing sketch Simplified_Circuit (saved by Fritzing 0.9.2b)
breadboards: 1

parts:
  U1 = attiny85 [package=dip]
  S1 = Momentary Switch [package=ksa_sealed_tac_switch]
  R1 = PHOTOCELL [package=photocell-kit]
  LED1 = LEDs [package=led10mm]
  R2 = Resistor [tolerance=±5% resistance=220 package="0603 [SMD]"]
  R3 = Resistor [tolerance=±5% resistance=10k package="0402 [SMD]"]

nets:
  N1: U1.Pin_2, S1.1, S1.2
  N2: U1.Pin_3, R1.P$1, R3.Pin_0
  N3: U1.Pin_4, S1.3, S1.4, R1.P$2, R2.Pin_1
  N4: U1.Pin_5, LED1.A
  N5: U1.Pin_8, R3.Pin_1
  N6: LED1.C, R2.Pin_0
